// Logisim project RAM512Lib.circ as structural Verilog: 1 circuit, main circuit RAM512
module RAM512 (
  input  load,
  input  clk,
  input  [15:0] din,
  input  [8:0] ain,
  output [15:0] dout
);

  wire demultiplexer_1_out0, demultiplexer_1_out1;
  wire [7:0] ram_1_data, ram_2_data, ram_3_data, ram_4_data;

  Demultiplexer #(.enable("false")) demultiplexer_1 (
    .out0(demultiplexer_1_out0), .out1(demultiplexer_1_out1), .in(load), .sel(ain[8]));
  RAM #(.bus("separate")) ram_1 (
    .addr(ain[7:0]), .din(din[15:8]), .data(ram_1_data), .str(demultiplexer_1_out0), .clk(clk));  // open: sel, ld, clr
  RAM #(.bus("separate")) ram_2 (
    .addr(ain[7:0]), .din(din[15:8]), .data(ram_2_data), .str(demultiplexer_1_out1), .clk(clk));  // open: sel, ld, clr
  RAM #(.bus("separate")) ram_3 (
    .addr(ain[7:0]), .din(din[7:0]), .data(ram_3_data), .str(demultiplexer_1_out0), .clk(clk));  // open: sel, ld, clr
  RAM #(.bus("separate")) ram_4 (
    .addr(ain[7:0]), .din(din[7:0]), .data(ram_4_data), .str(demultiplexer_1_out1), .clk(clk));  // open: sel, ld, clr
  Multiplexer #(.width(16), .enable("false")) multiplexer_1 (
    .in0({ram_1_data, ram_3_data}), .in1({ram_2_data, ram_4_data}), .out(dout), .sel(ain[8]));
endmodule
