// Logisim project Add16Lib.circ as structural Verilog: 1 circuit, main circuit Add16
module Add16 (
  input  [15:0] b,
  input  [15:0] a,
  output [15:0] o
);

  wire fulladder_1_carry, fulladder_2_carry, fulladder_3_carry, fulladder_4_carry, fulladder_5_carry,
       fulladder_6_carry, fulladder_7_carry, fulladder_8_carry, fulladder_9_carry, fulladder_10_carry,
       fulladder_11_carry, fulladder_12_carry, fulladder_13_carry, fulladder_14_carry, halfadder_1_carry;

  HalfAdder halfadder_1 (.a(a[0]), .b(b[0]), .sum(o[0]), .carry(halfadder_1_carry));
  FullAdder fulladder_1 (.a(a[1]), .b(b[1]), .c(halfadder_1_carry), .sum(o[1]), .carry(fulladder_1_carry));
  FullAdder fulladder_2 (.a(a[2]), .b(b[2]), .c(fulladder_1_carry), .sum(o[2]), .carry(fulladder_2_carry));
  FullAdder fulladder_3 (.a(a[3]), .b(b[3]), .c(fulladder_2_carry), .sum(o[3]), .carry(fulladder_3_carry));
  FullAdder fulladder_4 (.a(a[4]), .b(b[4]), .c(fulladder_3_carry), .sum(o[4]), .carry(fulladder_4_carry));
  FullAdder fulladder_5 (.a(a[5]), .b(b[5]), .c(fulladder_4_carry), .sum(o[5]), .carry(fulladder_5_carry));
  FullAdder fulladder_6 (.a(a[6]), .b(b[6]), .c(fulladder_5_carry), .sum(o[6]), .carry(fulladder_6_carry));
  FullAdder fulladder_7 (.a(a[7]), .b(b[7]), .c(fulladder_6_carry), .sum(o[7]), .carry(fulladder_7_carry));
  FullAdder fulladder_8 (.a(a[8]), .b(b[8]), .c(fulladder_7_carry), .sum(o[8]), .carry(fulladder_8_carry));
  FullAdder fulladder_9 (.a(a[9]), .b(b[9]), .c(fulladder_8_carry), .sum(o[9]), .carry(fulladder_9_carry));
  FullAdder fulladder_10 (.a(a[10]), .b(b[10]), .c(fulladder_9_carry), .sum(o[10]), .carry(fulladder_10_carry));
  FullAdder fulladder_11 (.a(a[11]), .b(b[11]), .c(fulladder_10_carry), .sum(o[11]), .carry(fulladder_11_carry));
  FullAdder fulladder_12 (.a(a[12]), .b(b[12]), .c(fulladder_11_carry), .sum(o[12]), .carry(fulladder_12_carry));
  FullAdder fulladder_13 (.a(a[13]), .b(b[13]), .c(fulladder_12_carry), .sum(o[13]), .carry(fulladder_13_carry));
  FullAdder fulladder_14 (.a(a[14]), .b(b[14]), .c(fulladder_13_carry), .sum(o[14]), .carry(fulladder_14_carry));
  FullAdder fulladder_15 (.a(a[15]), .b(b[15]), .c(fulladder_14_carry), .sum(o[15]));  // open: carry
endmodule
