// Logisim project BitLib.circ as structural Verilog: 1 circuit, main circuit Bit
module Bit (
  input  clk,
  input  i,
  input  load,
  output o
);

  wire multiplexer_1_out;

  Multiplexer #(.enable("false")) multiplexer_1 (.in0(o), .in1(i), .out(multiplexer_1_out), .sel(load));
  D_Flip_Flop d_ff_1 (.clk(clk), .D(multiplexer_1_out), .Q(o), .preset(1'b0), .reset(1'b0));  // open: Qn, en
endmodule
