// Logisim project CPULib.circ as structural Verilog: 9 circuits, main circuit CPU
module CPU (
  input  [15:0] ins,
  input  [15:0] inM,
  input  reset,
  input  clk,
  output [15:0] outM,
  output writeM,
  output [15:0] addressM,
  output [15:0] pgmCtr,
  output f
);

  wire aluammuxctl_1_o, aregloadctl_1_o, aregmuxctl_1_o, dregloadctl_1_o, ng, pcincctl_1_o, pcloadctl_1_o, zr;
  wire [15:0] multiplexer_1_out, multiplexer_2_out, outD;

  Multiplexer #(.width(16), .enable("false")) multiplexer_1 (
    .in0(ins), .in1(outM), .out(multiplexer_1_out), .sel(aregmuxctl_1_o));
  ARegMuxCtl aregmuxctl_1 (.instIn(ins), .o(aregmuxctl_1_o));
  ARegLoadCtl aregloadctl_1 (.instIn(ins), .o(aregloadctl_1_o));
  DRegLoadCtl dregloadctl_1 (.instIn(ins), .o(dregloadctl_1_o));
  PCLoadCtl pcloadctl_1 (.ins(ins), .zr(zr), .ng(ng), .o(pcloadctl_1_o));
  PCIncCtl pcincctl_1 (.reset(reset), .pcload(pcloadctl_1_o), .o(pcincctl_1_o));
  Reg16 A (.load(aregloadctl_1_o), .clk(clk), .D(multiplexer_1_out), .Q(addressM));
  Reg16 D (.load(dregloadctl_1_o), .clk(clk), .D(outM), .Q(outD));
  Multiplexer #(.width(16), .enable("false")) multiplexer_2 (
    .in0(addressM), .in1(inM), .out(multiplexer_2_out), .sel(aluammuxctl_1_o));
  PC PC (.i(addressM), .inc(pcincctl_1_o), .load(pcloadctl_1_o), .reset(reset), .clk(clk), .o(pgmCtr));
  ALUAMMuxCtl aluammuxctl_1 (.instIn(ins), .o(aluammuxctl_1_o));
  ALU ALU (
    .x(outD), .y(multiplexer_2_out), .zx(ins[11]), .zy(ins[9]), .no(ins[6]), .nx(ins[10]), .ny(ins[8]),
    .f(ins[7]), .o(outM), .zr(zr), .ng(ng));
  WriteMCtl writemctl_1 (.ins(ins), .o(writeM));

  assign f = ins[7];

  // Other names for the same wires on the sheet: clock = clk; outA[15:0] = addressM
endmodule

module ARegMuxCtl (
  input  [15:0] instIn,
  output o
);


  assign o = instIn[15];
endmodule

module ARegLoadCtl (
  input  [15:0] instIn,
  output o
);

  wire and_1_out, not_1_out;

  not not_1 (not_1_out, instIn[15]);
  and and_1 (and_1_out, instIn[5], instIn[15]);
  or or_1 (o, and_1_out, not_1_out);

  // Notes on the sheet:
  //   ~i or (i and d1)
endmodule

module ALUAMMuxCtl (
  input  [15:0] instIn,
  output o
);

  and and_1 (o, instIn[12], instIn[15]);

  // Notes on the sheet:
  //   i and a
endmodule

module DRegLoadCtl (
  input  [15:0] instIn,
  output o
);

  and and_1 (o, instIn[4], instIn[15]);

  // Notes on the sheet:
  //   i and d2
endmodule

module WriteMCtl (
  input  [15:0] ins,
  output o
);

  and and_1 (o, ins[3], ins[15]);

  // Notes on the sheet:
  //   i and d3
endmodule

module PCLoadCtl (
  input  [15:0] ins,
  input  zr,
  input  ng,
  output o
);

  wire jeq_out, jge_out, jgt_out, jle_out, jlt_out, jmp_out, jne_out, notj1, notj2, notj3, notng, notzr,
       or_1_out, or_2_out, or_3_out;

  not not_1 (notzr, zr);
  not not_2 (notng, ng);
  not not_3 (notj3, ins[0]);
  not not_4 (notj2, ins[1]);
  not not_5 (notj1, ins[2]);
  or or_1 (or_1_out, zr, notng);
  and jgt (jgt_out, notj1, notj2, ins[0], notzr, notng);
  and jeq (jeq_out, notj1, ins[1], notj3, zr);
  and jge (jge_out, notj1, ins[1], ins[0], or_1_out);
  and jlt (jlt_out, ins[2], notj2, notj3, notzr, ng);
  or or_2 (or_2_out, zr, ng);
  and jne (jne_out, ins[2], notj2, ins[0], notzr);
  and jle (jle_out, ins[2], ins[1], notj3, or_2_out);
  and jmp (jmp_out, ins[2], ins[1], ins[0]);
  or or_3 (or_3_out, jgt_out, jne_out, jeq_out, jle_out, jge_out, jmp_out, jlt_out);
  and and_1 (o, ins[15], or_3_out);

  // Other names for the same wires on the sheet: j3 = ins[0]; j2 = ins[1]; j1 = ins[2]; i = ins[15]
endmodule

module PCIncCtl (
  input  reset,
  input  pcload,
  output o
);

  and and_1 (o, ~reset, ~pcload);  // AND_Gate
endmodule

module CPUPCTst (
  input  in_1,
  output [15:0] data_out_to_RAM__D__A,
  output [15:0] address_out_to_RAM,
  output [15:0] program_counter
);

  wire clk, cpu_1_f, cpu_1_writem;
  wire [15:0] ram_1_data, rom_1_data;

  Clock clock_1 (.out(clk));
  ROM #(.addrWidth(15), .dataWidth(16)) rom_1 (.addr(program_counter[14:0]), .data(rom_1_data));  // open: sel
  CPU cpu_1 (
    .ins(rom_1_data), .inM(ram_1_data), .clk(clk), .reset(in_1), .outM(data_out_to_RAM__D__A),
    .writeM(cpu_1_writem), .addressM(address_out_to_RAM), .pgmCtr(program_counter), .f(cpu_1_f));
  LED led_1 (.in(cpu_1_writem));
  LED led_2 (.in(cpu_1_f));
  RAM #(.addrWidth(14), .dataWidth(16), .bus("separate")) ram_1 (
    .addr(address_out_to_RAM[13:0]), .din(data_out_to_RAM__D__A), .data(ram_1_data), .str(cpu_1_writem),
    .clk(clk));  // open: sel, ld, clr

  // Notes on the sheet:
  //   contents of rom_1 (hex, n*v repeats v):
  //   0 fc10 1 f4d0 a e301 1 fc10 c ea87 0 fc10 2 e308 e ea87
endmodule
