// Logisim project CPULib.circ as structural Verilog: 17 circuits, main circuit CPU
module CPU (
  input  reset,
  output writeM
);

  wire A, a_t, clock, dIn, enALU, IR, jIn, lMux, load, loadA, loadD, loadM, ng, PCIn, pcincctl_1_o,
       pcloadctl_1_o, res, zr;
  wire [5:0] ALU;
  wire [14:0] AIn, jIns, PC2, register_2_q, romsel_1_out_5;
  wire [14:11] rom_2_data;
  wire [15:0] addressM, dIns, inM, ins, is, jsel_1_o, multiplexer_1_out, multiplexer_2_out,
       multiplexer_3_out, outA, outD, outM, PCI, pgmCtr, register_3_q, rom_1_data, sel;

  Clock clock_1 (.out(clock));
  // Probe on multiplexer_2_out
  Multiplexer #(.width(16), .enable("false")) multiplexer_1 (
    .in1({is[15:13], a_t, is[11:0]}), .out(multiplexer_1_out), .sel(load));  // open: in0
  // Probe on inM
  ROMSel romsel_1 (.in_1(PC2), .in_2(jIns), ._0(PCIn), .Jin(jIn), .out_5(romsel_1_out_5));
  Multiplexer #(.width(16), .enable("false")) multiplexer_2 (
    .in0(multiplexer_1_out), .in1(outM), .out(multiplexer_2_out), .sel(A));
  Register #(.width(16)) register_1 (
    .D(rom_1_data), .en(IR), .Q({is[15:13], a_t, is[11:0]}), .clk(clock));  // open: clr
  ROM #(.addrWidth(15), .dataWidth(16)) rom_1 (.addr(register_2_q), .data(rom_1_data));  // open: sel
  Register #(.width(15)) register_2 (.D(romsel_1_out_5), .en(PCIn), .Q(register_2_q), .clk(clock));  // open: clr
  Adder #(.width(15)) adder_1 (.a(register_2_q), .b(15'h1), .out(PC2));  // open: cin, cout
  LED led_1 (.in(loadM));
  PCLoadCtl pcloadctl_1 (.ins(ins), .zr(zr), .ng(ng), .o(pcloadctl_1_o));
  PCIncCtl pcincctl_1 (.reset(reset), .pcload(pcloadctl_1_o), .o(pcincctl_1_o));
  ADir adir_1 (.ADir(outA), .AIn(AIn));
  Reg16 u_A (.load(loadA), .clk(clock), .D(multiplexer_2_out), .Q(outA));
  Reg16 D (.load(loadD), .clk(clock), .D(outM), .Q(outD));
  // Probe on inM
  RAM #(.addrWidth(14), .dataWidth(16), .bus("separate")) ram_1 (
    .addr(addressM[13:0]), .din(outM), .data(inM), .str(loadM), .clk(clock));  // open: sel, ld, clr
  Multiplexer #(.width(16), .enable("false")) multiplexer_3 (.in0(outA), .in1(inM), .out(multiplexer_3_out), .sel(a_t));
  // Probe on outD
  PC PC (.i(outA), .inc(pcincctl_1_o), .load(pcloadctl_1_o), .reset(reset), .clk(clock), .o(pgmCtr));
  // Probe on pgmCtr
  // Probe on multiplexer_3_out
  // Probe on jsel_1_o
  JSel jsel_1 (.PCI(PCI), .sel(sel), .dBit(dIns), .IMux(lMux), .dIn(dIn), .O(jsel_1_o));
  ALU u_ALU (
    .x(outD), .y(multiplexer_3_out), .zx(ALU[5]), .zy(ALU[3]), .no(ALU[0]), .nx(ALU[4]), .ny(ALU[2]),
    .f(ALU[1]), .o(outM), .zr(zr), .ng(ng));
  Register #(.width(16)) register_3 (.D(jsel_1_o), .Q(register_3_q), .clk(clock), .clr(res));  // open: en
  Adder #(.width(16)) adder_2 (.a(register_3_q), .b(16'h1), .out(PCI));  // open: cin, cout
  // Probe on outM
  WriteMCtl writemctl_1 (.ins(ins), .o(writeM));
  AregAdd aregadd_1 (.outA(outA), .outA_2(outA), .a(a_t), .A_2(A), .addressM(addressM));
  ROM #(.addrWidth(16), .dataWidth(16)) rom_2 (
    .addr(register_3_q),
    .data({res, rom_2_data, A, jIn, loadM, loadD, loadA, dIn, enALU, load, lMux, PCIn, IR}));  // open: sel
  instT instt_1 (.in_1(is[15]), .in_2(is[15]), .sel(sel));
  // Probe on jIns
  jIns jins_1 (.AIn(AIn), .zr(zr), .ng(ng), .j1(is[0]), .j2(is[1]), .j3(is[2]), .jIns(jIns));
  dIns dins_1 (.d1(is[3]), .d2(is[4]), .d3(is[5]), .dIns(dIns));
  // Probe on ALU
  Multiplexer #(.width(6), .enable("false")) multiplexer_4 (.in1(is[11:6]), .out(ALU), .sel(enALU));  // open: in0
  // Probe on dIns

  // Other names for the same wires on the sheet: f = ALU[1]; is[12] = a_t

  // Notes on the sheet:
  //   contents of rom_1 (hex, n*v repeats v):
  //   8000 8008 8010 8018 8020 8028 8030 8038
  //   contents of rom_2 (hex, n*v repeats v):
  //   0 1 3 4 17*0 48 8000 18*0 10 30 212 8000 0 510 212 8000 0 0 90 212 8000 0 0 590 212 8000 0 0 450 212
  //   8000 7*0 4d0 212 8000 0 0 5d0 212 8000 23*0 550 212 8000
endmodule

module ARegMuxCtl (
  input  [15:0] instIn,
  output o
);


  assign o = instIn[15];
endmodule

module ARegLoadCtl (
  input  [15:0] instIn,
  output o
);

  wire and_1_out, not_1_out;

  not not_1 (not_1_out, instIn[15]);
  and and_1 (and_1_out, instIn[5], instIn[15]);
  or or_1 (o, and_1_out, not_1_out);

  // Notes on the sheet:
  //   ~i or (i and d1)
endmodule

module ALUAMMuxCtl (
  input  [15:0] instIn,
  output o
);

  and and_1 (o, instIn[12], instIn[15]);

  // Notes on the sheet:
  //   i and a
endmodule

module DRegLoadCtl (
  input  [15:0] instIn,
  output o
);

  and and_1 (o, instIn[4], instIn[15]);

  // Notes on the sheet:
  //   i and d2
endmodule

module WriteMCtl (
  input  [15:0] ins,
  output o
);

  and and_1 (o, ins[3], ins[15]);

  // Notes on the sheet:
  //   i and d3
endmodule

module PCLoadCtl (
  input  [15:0] ins,
  input  zr,
  input  ng,
  output o
);

  wire jeq_out, jge_out, jgt_out, jle_out, jlt_out, jmp_out, jne_out, notj1, notj2, notj3, notng, notzr,
       or_1_out, or_2_out, or_3_out;

  not not_1 (notzr, zr);
  not not_2 (notng, ng);
  not not_3 (notj3, ins[0]);
  not not_4 (notj2, ins[1]);
  not not_5 (notj1, ins[2]);
  or or_1 (or_1_out, zr, notng);
  and jgt (jgt_out, notj1, notj2, ins[0], notzr, notng);
  and jeq (jeq_out, notj1, ins[1], notj3, zr);
  and jge (jge_out, notj1, ins[1], ins[0], or_1_out);
  and jlt (jlt_out, ins[2], notj2, notj3, notzr, ng);
  or or_2 (or_2_out, zr, ng);
  and jne (jne_out, ins[2], notj2, ins[0], notzr);
  and jle (jle_out, ins[2], ins[1], notj3, or_2_out);
  and jmp (jmp_out, ins[2], ins[1], ins[0]);
  or or_3 (or_3_out, jgt_out, jne_out, jeq_out, jle_out, jge_out, jmp_out, jlt_out);
  and and_1 (o, ins[15], or_3_out);

  // Other names for the same wires on the sheet: j3 = ins[0]; j2 = ins[1]; j1 = ins[2]; i = ins[15]
endmodule

module PCIncCtl (
  input  reset,
  input  pcload,
  output o
);

  and and_1 (o, ~reset, ~pcload);  // AND_Gate
endmodule

module CPUPCTst (
  input  in_1,
  output [15:0] data_out_to_RAM__D__A,
  output [15:0] address_out_to_RAM,
  output [15:0] program_counter
);

  wire clk, cpu_1_p6, undriven;
  wire [15:0] cpu_1_p2, rom_1_data;

  Clock clock_1 (.out(clk));
  ROM #(.addrWidth(15), .dataWidth(16)) rom_1 (.addr(program_counter[14:0]), .data(rom_1_data));  // open: sel
  // CPU cpu_1: pin names not known; wires that end beside it: rom_1_data, cpu_1_p2, clk, in_1, data_out_to_RAM__D__A, cpu_1_p6, address_out_to_RAM, program_counter
  LED led_1 (.in(cpu_1_p6));
  LED led_2 (.in(undriven));
  RAM #(.addrWidth(14), .dataWidth(16), .bus("separate")) ram_1 (
    .addr(address_out_to_RAM[13:0]), .din(data_out_to_RAM__D__A), .data(cpu_1_p2), .str(cpu_1_p6), .clk(clk));  // open: sel, ld, clr

  // Notes on the sheet:
  //   contents of rom_1 (hex, n*v repeats v):
  //   0 fc10 1 f4d0 a e301 1 fc10 c ea87 0 fc10 2 e308 e ea87
endmodule

module CON (
);

  Counter counter_1 ();  // open: load, D, count, Q, carry, clk, clr
  ROM rom_1 ();  // open: addr, data, sel
endmodule

module instT (
  input  in_1,
  input  in_2,
  output [15:0] sel
);

  wire A, C;

  Demultiplexer #(.enable("false")) demultiplexer_1 (.out0(A), .out1(C), .in(1'b1), .sel(in_1));
  // Probe on sel
  Multiplexer #(.width(16), .enable("false")) multiplexer_1 (.in0(16'h14), .in1(16'h28), .out(sel), .sel(in_2));
endmodule

module dIns (
  input  d1,
  input  d2,
  input  d3,
  output [15:0] dIns
);

  wire A_out, AD_out, ADM_out, AM_out, D_out, DM_out, M_2_out, M_out, notd1, notd2, notd3;

  not not_1 (notd1, d1);
  not not_2 (notd2, d2);
  not not_3 (notd3, d3);
  Multiplexer #(.width(16), .enable("false")) multiplexer_1 (.in1(16'h2b), .out(dIns), .sel(M_out));  // open: in0
  and M (M_out, notd1, notd2, notd3);
  Multiplexer #(.width(16), .enable("false")) multiplexer_2 (.in1(16'h2d), .out(dIns), .sel(M_2_out));  // open: in0
  and M_2 (M_2_out, d1, notd2, notd3);
  // Probe on nothing
  Multiplexer #(.width(16), .enable("false")) multiplexer_3 (.in1(16'h32), .out(dIns), .sel(D_out));  // open: in0
  and D (D_out, notd1, d2, notd3);
  Multiplexer #(.width(16), .enable("false")) multiplexer_4 (.in1(16'h37), .out(dIns), .sel(DM_out));  // open: in0
  and DM (DM_out, d1, d2, notd3);
  Multiplexer #(.width(16), .enable("false")) multiplexer_5 (.in1(16'h3c), .out(dIns), .sel(A_out));  // open: in0
  and A (A_out, notd1, notd2, d3);
  and AM (AM_out, d1, notd2, d3);
  and AD (AD_out, notd1, d2, d3);
  and ADM (ADM_out, d1, d2, d3);
  Multiplexer #(.width(16), .enable("false")) multiplexer_6 (.in1(16'h65), .out(dIns), .sel(AM_out));  // open: in0
  Multiplexer #(.width(16), .enable("false")) multiplexer_7 (.in1(16'h46), .out(dIns), .sel(AD_out));  // open: in0
  Multiplexer #(.width(16), .enable("false")) multiplexer_8 (.in1(16'h4b), .out(dIns), .sel(ADM_out));  // open: in0
endmodule

module JSel (
  input  [15:0] PCI,
  input  [15:0] sel,
  input  [15:0] dBit,
  input  IMux,
  input  dIn,
  output [15:0] O
);

  wire [15:0] multiplexer_1_out;

  Multiplexer #(.width(16), .enable("false")) multiplexer_1 (.in0(PCI), .in1(sel), .out(multiplexer_1_out), .sel(IMux));
  Multiplexer #(.width(16), .enable("false")) multiplexer_2 (.in0(multiplexer_1_out), .in1(dBit), .out(O), .sel(dIn));
endmodule

module jIns (
  input  [14:0] AIn,
  input  zr,
  input  ng,
  input  j1,
  input  j2,
  input  j3,
  output [14:0] jIns
);

  wire jeq_out, jge_out, jgt_out, jle_out, jlt_out, jmp_out, jne_out, notj1, notj2, notj3, notng, notzr,
       or_1_out, or_2_out;

  not not_1 (notzr, zr);
  not not_2 (notng, ng);
  not not_3 (notj1, j1);
  not not_4 (notj2, j2);
  not not_5 (notj3, j3);
  or or_1 (or_1_out, zr, notng);
  Multiplexer #(.width(15), .enable("false")) multiplexer_1 (.in1(AIn), .out(jIns), .sel(jgt_out));  // open: in0
  and jgt (jgt_out, j1, notj2, notj3, notzr, notng);
  Multiplexer #(.width(15), .enable("false")) multiplexer_2 (.in1(AIn), .out(jIns), .sel(jeq_out));  // open: in0
  and jeq (jeq_out, notj1, j2, notj3, zr);
  Multiplexer #(.width(15), .enable("false")) multiplexer_3 (.in1(AIn), .out(jIns), .sel(jge_out));  // open: in0
  and jge (jge_out, j1, j2, notj3, or_1_out);
  and jlt (jlt_out, notj1, notj2, j3, notzr, ng);
  Multiplexer #(.width(15), .enable("false")) multiplexer_4 (.in1(AIn), .out(jIns), .sel(jlt_out));  // open: in0
  or or_2 (or_2_out, zr, ng);
  and jne (jne_out, j1, notj2, j3, notzr);
  and jle (jle_out, notj1, j2, j3, or_2_out);
  and jmp (jmp_out, j1, j2, j3);
  Multiplexer #(.width(15), .enable("false")) multiplexer_5 (.in1(AIn), .out(jIns), .sel(jne_out));  // open: in0
  Multiplexer #(.width(15), .enable("false")) multiplexer_6 (.in1(AIn), .out(jIns), .sel(jle_out));  // open: in0
  Multiplexer #(.width(15), .enable("false")) multiplexer_7 (.in1(AIn), .out(jIns), .sel(jmp_out));  // open: in0
endmodule

module ROMSel (
  input  [14:0] in_1,
  input  [14:0] in_2,
  input  _0,
  input  Jin,
  output [14:0] out_5
);

  wire [14:0] multiplexer_1_out;

  Multiplexer #(.width(15), .enable("false")) multiplexer_1 (
    .in1(in_1), .out(multiplexer_1_out), .sel(_0));  // open: in0
  Multiplexer #(.width(15), .enable("false")) multiplexer_2 (
    .in0(multiplexer_1_out), .in1(in_2), .out(out_5), .sel(Jin));
endmodule

module AregAdd (
  input  [15:0] outA,
  input  [15:0] outA_2,
  input  a,
  input  A_2,
  output [15:0] addressM
);

  wire [15:0] multiplexer_1_out;

  Multiplexer #(.width(16), .enable("false")) multiplexer_1 (
    .in1(outA), .out(multiplexer_1_out), .sel(a));  // open: in0
  Multiplexer #(.width(16), .enable("false")) multiplexer_2 (
    .in0(multiplexer_1_out), .in1(outA_2), .out(addressM), .sel(A_2));
endmodule

module ADir (
  input  [15:0] ADir,
  output [14:0] AIn
);


  assign AIn = ADir[14:0];
endmodule
