// Logisim project Esquema inicial.circ as structural Verilog: 1 circuit, main circuit main
module main (
  input  [15:0] ins,
  input  [15:0] inM,
  input  writeM,
  input  reset,
  input  clk,
  output [15:0] outM,
  output [15:0] addressM,
  output [15:0] PCntr
);

  ROM #(.addrWidth(15), .dataWidth(16)) rom_1 ();  // open: addr, data, sel
  // Reg16 A: pin names not known
  // Reg16 D: pin names not known
  // PC PC: pin names not known
  // ALU ALU: pin names not known
  RAM #(.addrWidth(14), .dataWidth(16)) ram_1 ();  // open: addr, data, sel, clk, ld, clr

  // Notes on the sheet:
  //   ROM32k 
  //   RAM16k
endmodule
