// Logisim project FullAdderLib.circ as structural Verilog: 1 circuit, main circuit FullAdder
module FullAdder (
  input  a,
  input  b,
  input  c,
  output sum,
  output carry
);

  wire and_1_out, and_2_out, halfadder_1_sum;

  HalfAdder halfadder_1 (.a(a), .b(b), .sum(halfadder_1_sum));  // open: carry
  xor xor_1 (sum, halfadder_1_sum, c);
  and and_1 (and_1_out, halfadder_1_sum, c);
  and and_2 (and_2_out, a, b);
  or or_1 (carry, and_1_out, and_2_out);
endmodule
