// Logisim project HalfAdderLib.circ as structural Verilog: 1 circuit, main circuit HalfAdder
module HalfAdder (
  input  a,
  input  b,
  output sum,
  output carry
);

  xor xor_1 (sum, a, b);
  and and_1 (carry, a, b);
endmodule
