// Logisim project Inc16Lib.circ as structural Verilog: 1 circuit, main circuit Add16
module Add16 (
  input  [15:0] a,
  output [15:0] out_2
);

  Add16Lib_Add16 add16_1 (.b(a), .a(16'h1), .o(out_2));
endmodule
