// Logisim project PCLib.circ as structural Verilog: 1 circuit, main circuit PC
module PC (
  input  inc,
  input  load,
  input  reset,
  input  clk,
  input  [15:0] i,
  output [15:0] o
);

  wire or_1_out;
  wire [15:0] add16_1_out_2, multiplexer_1_out, multiplexer_2_out, multiplexer_3_out;

  Multiplexer #(.width(16), .enable("false")) multiplexer_1 (
    .in1(add16_1_out_2), .out(multiplexer_1_out), .sel(inc));  // open: in0
  Multiplexer #(.width(16), .enable("false")) multiplexer_2 (
    .in0(multiplexer_1_out), .in1(i), .out(multiplexer_2_out), .sel(load));
  or or_1 (or_1_out, inc, load, reset);
  Multiplexer #(.width(16), .enable("false")) multiplexer_3 (
    .in0(multiplexer_2_out), .in1({16{1'b0}}), .out(multiplexer_3_out), .sel(reset));
  Reg16 reg16_1 (.load(or_1_out), .clk(clk), .D(multiplexer_3_out), .Q(o));
  Add16 add16_1 (.a(o), .out_2(add16_1_out_2));
endmodule
