// Logisim project RAM16kLib.circ as structural Verilog: 1 circuit, main circuit RAM16k
module RAM16k (
  input  [15:0] din,
  input  [13:0] ain,
  input  clk,
  input  load,
  output [15:0] dout
);

  RAM #(.addrWidth(14), .dataWidth(16), .bus("separate")) ram_1 (
    .addr(ain), .din(din), .data(dout), .str(load), .clk(clk));  // open: sel, ld, clr
endmodule
