// Logisim project RAM64Lib.circ as structural Verilog: 1 circuit, main circuit RAM64
module RAM64 (
  input  clk,
  input  load,
  input  [5:0] ain,
  input  [15:0] D,
  output [15:0] Q
);

  wire demultiplexer_1_out0, demultiplexer_1_out1, demultiplexer_1_out2, demultiplexer_1_out3,
       demultiplexer_1_out4, demultiplexer_1_out5, demultiplexer_1_out6, demultiplexer_1_out7;
  wire [15:0] ram8_1_q, ram8_2_q, ram8_3_q, ram8_4_q, ram8_5_q, ram8_6_q, ram8_7_q, ram8_8_q;

  Demultiplexer #(.select(3), .enable("false")) demultiplexer_1 (
    .out0(demultiplexer_1_out0), .out1(demultiplexer_1_out1), .out2(demultiplexer_1_out2),
    .out3(demultiplexer_1_out3), .out4(demultiplexer_1_out4), .out5(demultiplexer_1_out5),
    .out6(demultiplexer_1_out6), .out7(demultiplexer_1_out7), .in(load), .sel(ain[5:3]));
  RAM8 ram8_1 (.clk(clk), .load(demultiplexer_1_out0), .ain(ain[2:0]), .D(D), .Q(ram8_1_q));
  RAM8 ram8_2 (.clk(clk), .load(demultiplexer_1_out1), .ain(ain[2:0]), .D(D), .Q(ram8_2_q));
  RAM8 ram8_3 (.clk(clk), .load(demultiplexer_1_out2), .ain(ain[2:0]), .D(D), .Q(ram8_3_q));
  RAM8 ram8_4 (.clk(clk), .load(demultiplexer_1_out3), .ain(ain[2:0]), .D(D), .Q(ram8_4_q));
  RAM8 ram8_5 (.clk(clk), .load(demultiplexer_1_out4), .ain(ain[2:0]), .D(D), .Q(ram8_5_q));
  RAM8 ram8_6 (.clk(clk), .load(demultiplexer_1_out5), .ain(ain[2:0]), .D(D), .Q(ram8_6_q));
  RAM8 ram8_7 (.clk(clk), .load(demultiplexer_1_out6), .ain(ain[2:0]), .D(D), .Q(ram8_7_q));
  RAM8 ram8_8 (.clk(clk), .load(demultiplexer_1_out7), .ain(ain[2:0]), .D(D), .Q(ram8_8_q));
  Multiplexer #(.select(3), .width(16), .enable("false")) multiplexer_1 (
    .in0(ram8_1_q), .in1(ram8_2_q), .in2(ram8_3_q), .in3(ram8_4_q), .in4(ram8_5_q), .in5(ram8_6_q),
    .in6(ram8_7_q), .in7(ram8_8_q), .out(Q), .sel(ain[5:3]));

  // Other names for the same wires on the sheet: ain_t[2:0] = ain[5:3]
endmodule
