// Logisim project RAM8Lib.circ as structural Verilog: 1 circuit, main circuit RAM8
module RAM8 (
  input  clk,
  input  load,
  input  [2:0] ain,
  input  [15:0] D,
  output [15:0] Q
);

  wire demultiplexer_1_out0, demultiplexer_1_out1, demultiplexer_1_out2, demultiplexer_1_out3,
       demultiplexer_1_out4, demultiplexer_1_out5, demultiplexer_1_out6, demultiplexer_1_out7;
  wire [15:0] reg16_1_q, reg16_2_q, reg16_3_q, reg16_4_q, reg16_5_q, reg16_6_q, reg16_7_q, reg16_8_q;

  Demultiplexer #(.select(3), .enable("false")) demultiplexer_1 (
    .out0(demultiplexer_1_out0), .out1(demultiplexer_1_out1), .out2(demultiplexer_1_out2),
    .out3(demultiplexer_1_out3), .out4(demultiplexer_1_out4), .out5(demultiplexer_1_out5),
    .out6(demultiplexer_1_out6), .out7(demultiplexer_1_out7), .in(load), .sel(ain));
  Reg16 reg16_1 (.load(demultiplexer_1_out0), .clk(clk), .D(D), .Q(reg16_1_q));
  Reg16 reg16_2 (.load(demultiplexer_1_out1), .clk(clk), .D(D), .Q(reg16_2_q));
  Reg16 reg16_3 (.load(demultiplexer_1_out2), .clk(clk), .D(D), .Q(reg16_3_q));
  Reg16 reg16_4 (.load(demultiplexer_1_out3), .clk(clk), .D(D), .Q(reg16_4_q));
  Reg16 reg16_5 (.load(demultiplexer_1_out4), .clk(clk), .D(D), .Q(reg16_5_q));
  Reg16 reg16_6 (.load(demultiplexer_1_out5), .clk(clk), .D(D), .Q(reg16_6_q));
  Reg16 reg16_7 (.load(demultiplexer_1_out6), .clk(clk), .D(D), .Q(reg16_7_q));
  Reg16 reg16_8 (.load(demultiplexer_1_out7), .clk(clk), .D(D), .Q(reg16_8_q));
  Multiplexer #(.select(3), .width(16), .enable("false")) multiplexer_1 (
    .in0(reg16_1_q), .in1(reg16_2_q), .in2(reg16_3_q), .in3(reg16_4_q), .in4(reg16_5_q), .in5(reg16_6_q),
    .in6(reg16_7_q), .in7(reg16_8_q), .out(Q), .sel(ain));
endmodule
