// Logisim project Reg16Lib.circ as structural Verilog: 1 circuit, main circuit Reg16
module Reg16 (
  input  load,
  input  clk,
  input  [15:0] D,
  output [15:0] Q
);

  Bit bit_1 (.clk(clk), .i(D[0]), .load(load), .o(Q[0]));
  Bit bit_2 (.clk(clk), .i(D[1]), .load(load), .o(Q[1]));
  Bit bit_3 (.clk(clk), .i(D[2]), .load(load), .o(Q[2]));
  Bit bit_4 (.clk(clk), .i(D[3]), .load(load), .o(Q[3]));
  Bit bit_5 (.clk(clk), .i(D[4]), .load(load), .o(Q[4]));
  Bit bit_6 (.clk(clk), .i(D[5]), .load(load), .o(Q[5]));
  Bit bit_7 (.clk(clk), .i(D[6]), .load(load), .o(Q[6]));
  Bit bit_8 (.clk(clk), .i(D[7]), .load(load), .o(Q[7]));
  Bit bit_9 (.clk(clk), .i(D[8]), .load(load), .o(Q[8]));
  Bit bit_10 (.clk(clk), .i(D[9]), .load(load), .o(Q[9]));
  Bit bit_11 (.clk(clk), .i(D[10]), .load(load), .o(Q[10]));
  Bit bit_12 (.clk(clk), .i(D[11]), .load(load), .o(Q[11]));
  Bit bit_13 (.clk(clk), .i(D[12]), .load(load), .o(Q[12]));
  Bit bit_14 (.clk(clk), .i(D[13]), .load(load), .o(Q[13]));
  Bit bit_15 (.clk(clk), .i(D[14]), .load(load), .o(Q[14]));
  Bit bit_16 (.clk(clk), .i(D[15]), .load(load), .o(Q[15]));
endmodule
